// Logisim project binary_counter.circ as structural Verilog: 1 circuit, main circuit main
module main (
  input  CLK,
  input  T0,
  output Q3,
  output Q2,
  output Q1,
  output Q0
);

  wire and_1_out, and_2_out, not_1_out, not_2_out, not_3_out, not_4_out, not_5_out, not_6_out;

  not not_1 (not_1_out, Q0);
  not not_2 (not_2_out, Q1);
  not not_3 (not_3_out, Q0);
  not not_4 (not_4_out, Q2);
  not not_5 (not_5_out, Q1);
  not not_6 (not_6_out, Q0);
  and and_1 (and_1_out, not_2_out, not_3_out);
  and and_2 (and_2_out, not_4_out, not_5_out, not_6_out);
  T_Flip_Flop t_ff_1 (.clk(CLK), .T(T0), .Q(Q0));  // open: Qn, preset, reset, en
  T_Flip_Flop t_ff_2 (.clk(CLK), .T(not_1_out), .Q(Q1));  // open: Qn, preset, reset, en
  T_Flip_Flop t_ff_3 (.clk(CLK), .T(and_1_out), .Q(Q2));  // open: Qn, preset, reset, en
  T_Flip_Flop t_ff_4 (.clk(CLK), .T(and_2_out), .Q(Q3));  // open: Qn, preset, reset, en
endmodule
