// Logisim project binary_evaluator.circ as structural Verilog: 2 circuits, main circuit SUB0
module SUB0 (
  input  A_0,
  input  B_0,
  input  Bin_0,
  output D_0,
  output Bout_0
);

  wire and_1_out, and_2_out, and_3_out, not_1_out, not_2_out, xor_1_out;

  xor xor_1 (xor_1_out, A_0, B_0);
  xor xor_2 (D_0, xor_1_out, Bin_0);
  not not_1 (not_1_out, A_0);
  not not_2 (not_2_out, A_0);
  and and_1 (and_1_out, not_1_out, B_0);
  and and_2 (and_2_out, not_2_out, Bin_0);
  and and_3 (and_3_out, B_0, Bin_0);
  or or_1 (Bout_0, and_1_out, and_2_out, and_3_out);
endmodule

module SUB1 (
  input  A_0,
  input  A_1,
  input  A_2,
  input  A_3,
  input  A_4,
  input  A_5,
  input  A_6,
  input  A_7,
  input  B_0,
  input  B_1,
  input  B_2,
  input  B_3,
  input  B_4,
  input  B_5,
  input  B_6,
  input  B_7,
  input  Bin_0,
  input  in_18,
  input  in_19,
  input  in_20,
  input  in_21,
  input  in_22,
  input  in_23,
  input  in_24,
  input  in_25,
  input  in_26,
  input  in_27,
  input  in_28,
  input  in_29,
  input  in_30,
  input  in_31,
  input  in_32,
  input  in_33,
  input  in_34,
  output D_0,
  output D_1,
  output D_2,
  output D_3,
  output D_4,
  output D_5,
  output D_6,
  output D_1_2,
  output Bout_0,
  output Bout_1,
  output Bout_2,
  output Bout_3,
  output Bout_4,
  output Bout_5,
  output Bout_6,
  output Bout_1_2,
  output out_51,
  output out_52,
  output out_53,
  output out_54,
  output out_55,
  output out_56,
  output out_57,
  output out_58
);

  wire xor_1_out, xor_2_out, xor_3_out, xor_4_out, xor_5_out, xor_6_out, xor_7_out, xor_9_out;

  xor xor_1 (xor_1_out, in_18, in_26);
  SUB0 sub0_1 (.A_0(A_0), .B_0(B_0), .Bin_0(Bin_0), .D_0(D_0), .Bout_0(Bout_0));
  xor xor_2 (xor_2_out, in_19, in_27);
  xor xor_3 (xor_3_out, in_20, in_28);
  xor xor_4 (xor_4_out, in_21, in_29);
  SUB0 sub0_2 (.A_0(A_1), .B_0(B_1), .Bin_0(Bout_0), .D_0(D_1), .Bout_0(Bout_1));
  xor xor_5 (xor_5_out, in_22, in_30);
  xor xor_6 (xor_6_out, in_23, in_31);
  xor xor_7 (xor_7_out, in_25, in_33);
  xor xor_8 (out_58, xor_7_out, out_57);
  xor xor_9 (xor_9_out, in_24, in_32);
  xor xor_10 (out_56, xor_6_out, out_55);
  xor xor_11 (out_57, xor_9_out, out_56);
  SUB0 sub0_3 (.A_0(A_2), .B_0(B_2), .Bin_0(Bout_1), .D_0(D_2), .Bout_0(Bout_2));
  xor xor_12 (out_55, xor_5_out, out_54);
  xor xor_13 (out_53, xor_3_out, out_52);
  xor xor_14 (out_54, xor_4_out, out_53);
  xor xor_15 (out_51, xor_1_out, in_34);
  xor xor_16 (out_52, xor_2_out, out_51);
  SUB0 sub0_4 (.A_0(A_3), .B_0(B_3), .Bin_0(Bout_2), .D_0(D_3), .Bout_0(Bout_3));
  SUB0 sub0_5 (.A_0(A_4), .B_0(B_4), .Bin_0(Bout_3), .D_0(D_4), .Bout_0(Bout_4));
  SUB0 sub0_6 (.A_0(A_5), .B_0(B_5), .Bin_0(Bout_4), .D_0(D_5), .Bout_0(Bout_5));
  SUB0 sub0_7 (.A_0(A_6), .B_0(B_6), .Bin_0(Bout_5), .D_0(D_6), .Bout_0(Bout_6));
  SUB0 sub0_8 (.A_0(A_7), .B_0(B_7), .Bin_0(Bout_6), .D_0(D_1_2), .Bout_0(Bout_1_2));
endmodule
