// Logisim project 4x_comp.circ as structural Verilog: 1 circuit, main circuit main
module main (
  input  A3,
  input  B3,
  input  A2,
  input  B2,
  input  A1,
  input  B1,
  input  A0,
  input  B0,
  output A___B,
  output out_10,
  output A___B_2
);

  wire and_1_out, and_2_out, and_3_out, and_4_out, and_5_out, and_6_out, and_7_out, and_8_out, and_9_out,
       and_10_out, and_11_out, and_12_out, and_13_out, and_14_out, not_1_out, not_2_out, not_3_out,
       not_4_out, not_5_out, not_6_out, not_7_out, not_8_out, or_1_out, or_2_out, or_3_out, or_4_out;

  not not_1 (not_1_out, A3);
  not not_2 (not_2_out, B3);
  not not_3 (not_3_out, A2);
  not not_4 (not_4_out, B2);
  not not_5 (not_5_out, A1);
  not not_6 (not_6_out, B1);
  not not_7 (not_7_out, A0);
  not not_8 (not_8_out, B0);
  and and_1 (and_1_out, not_1_out, B3);
  and and_2 (and_2_out, A3, not_2_out);
  and and_3 (and_3_out, not_3_out, B2);
  and and_4 (and_4_out, A2, not_4_out);
  and and_5 (and_5_out, not_5_out, B1);
  and and_6 (and_6_out, A1, not_6_out);
  and and_7 (and_7_out, not_7_out, B0);
  and and_8 (and_8_out, A0, not_8_out);
  or or_1 (or_1_out, and_1_out, and_2_out);
  or or_2 (or_2_out, and_3_out, and_4_out);
  or or_3 (or_3_out, and_5_out, and_6_out);
  or or_4 (or_4_out, and_7_out, and_8_out);
  and and_9 (and_9_out, or_1_out, and_3_out);
  and and_10 (and_10_out, or_1_out, and_4_out);
  and and_11 (and_11_out, or_1_out, or_2_out, and_5_out, and_5_out);
  and and_12 (and_12_out, or_1_out, or_2_out, and_6_out);
  and and_13 (and_13_out, or_1_out, or_2_out, or_3_out, and_7_out);
  and and_14 (and_14_out, or_1_out, or_2_out, or_3_out, and_8_out);
  and and_15 (A___B_2, or_1_out, or_2_out, or_3_out, or_4_out);
  or or_5 (A___B, and_1_out, and_9_out, and_11_out, and_13_out);
  or or_6 (out_10, and_10_out, and_2_out, and_12_out, and_14_out);

  // Notes on the sheet:
  //   A > B
endmodule
