// Logisim project 4x_comp_v2.circ as structural Verilog: 1 circuit, main circuit main
module main (
  input  A3,
  input  B3,
  input  A2,
  input  B2,
  input  A1,
  input  B1,
  input  A0,
  input  B0,
  output A___B,
  output A___B_2,
  output out_11,
  output out_12,
  output out_13
);

  wire and_1_out, and_2_out, and_3_out, and_4_out, and_5_out, and_6_out, and_7_out, and_8_out, and_9_out,
       and_10_out, and_11_out, and_12_out, and_13_out, and_14_out, and_15_out, and_16_out, and_17_out,
       and_18_out, and_19_out, and_20_out, and_21_out, and_22_out, and_23_out, and_24_out, and_25_out,
       and_26_out, and_27_out, and_28_out, and_29_out, and_30_out, and_31_out, and_32_out, and_33_out,
       and_34_out, and_35_out, and_36_out, and_37_out, and_38_out, and_39_out, and_40_out, and_41_out,
       and_42_out, and_43_out, and_44_out, and_45_out, and_46_out, and_47_out, and_48_out, and_49_out,
       and_50_out, and_51_out, and_52_out, and_53_out, and_54_out, not_1_out, not_2_out, not_3_out,
       not_4_out, not_5_out, not_6_out, not_7_out, not_8_out, not_9_out, not_10_out, not_11_out, not_12_out,
       not_13_out, not_14_out, not_15_out, not_16_out, not_17_out, not_18_out, not_19_out, not_20_out,
       not_21_out, not_22_out, not_23_out, not_24_out, not_25_out, not_26_out, not_27_out, not_28_out,
       not_29_out, not_30_out, not_31_out, not_32_out, not_33_out, not_34_out, not_35_out, not_36_out,
       not_37_out, not_38_out, not_39_out, not_40_out, not_41_out, not_42_out, not_43_out, not_44_out,
       not_45_out, not_46_out, not_47_out, not_48_out, or_1_out, or_2_out, or_3_out, or_4_out, or_5_out,
       or_6_out, or_7_out, or_8_out, or_9_out, or_10_out, or_11_out, or_12_out, or_13_out, or_14_out,
       or_15_out, or_17_out, or_19_out, or_20_out, or_21_out, or_23_out, or_24_out, undriven, undriven_2,
       undriven_3, undriven_4, undriven_5;

  not not_1 (not_1_out, A3);
  not not_2 (not_2_out, B3);
  not not_3 (not_3_out, A2);
  not not_4 (not_4_out, B2);
  not not_5 (not_5_out, A1);
  not not_6 (not_6_out, B1);
  not not_7 (not_7_out, A0);
  not not_8 (not_8_out, B0);
  not not_9 (not_9_out, undriven);
  not not_10 (not_10_out, undriven);
  and and_1 (and_1_out, not_1_out, not_2_out);
  and and_2 (and_2_out, A3, B3);
  and and_3 (and_3_out, not_3_out, not_4_out);
  and and_4 (and_4_out, A2, B2);
  and and_5 (and_5_out, not_5_out, not_6_out);
  and and_6 (and_6_out, A1, B1);
  and and_7 (and_7_out, not_7_out, not_8_out);
  and and_8 (and_8_out, A0, B0);
  not not_11 (not_11_out, undriven);
  buf and_9 (and_9_out, not_11_out);  // AND_Gate
  buf and_10 (and_10_out, not_9_out);  // AND_Gate
  buf and_11 (and_11_out, not_10_out);  // AND_Gate
  or or_1 (or_1_out, and_10_out, and_11_out);
  or or_2 (or_2_out, and_1_out, and_2_out);
  or or_3 (or_3_out, and_3_out, and_4_out);
  or or_4 (or_4_out, and_5_out, and_6_out);
  or or_5 (or_5_out, and_7_out, and_8_out);
  or or_6 (or_6_out, and_9_out, or_1_out);
  not not_12 (not_12_out, undriven_2);
  not not_13 (not_13_out, undriven_2);
  not not_14 (not_14_out, undriven_2);
  buf and_12 (and_12_out, not_12_out);  // AND_Gate
  not not_15 (not_15_out, B3);
  not not_16 (not_16_out, A3);
  not not_17 (not_17_out, A3);
  not not_18 (not_18_out, B3);
  not not_19 (not_19_out, B2);
  not not_20 (not_20_out, A2);
  not not_21 (not_21_out, A2);
  not not_22 (not_22_out, B2);
  not not_23 (not_23_out, B1);
  not not_24 (not_24_out, A1);
  not not_25 (not_25_out, A1);
  not not_26 (not_26_out, B1);
  not not_27 (not_27_out, B0);
  not not_28 (not_28_out, A0);
  not not_29 (not_29_out, A0);
  not not_30 (not_30_out, B0);
  not not_31 (not_31_out, or_2_out);
  not not_32 (not_32_out, or_3_out);
  not not_33 (not_33_out, or_4_out);
  not not_34 (not_34_out, or_5_out);
  buf and_13 (and_13_out, not_13_out);  // AND_Gate
  buf and_14 (and_14_out, not_14_out);  // AND_Gate
  and and_15 (and_15_out, A3, not_15_out);
  and and_16 (and_16_out, not_16_out, B3);
  and and_17 (and_17_out, B3, not_17_out);
  and and_18 (and_18_out, not_18_out, A3);
  and and_19 (and_19_out, A2, not_19_out);
  and and_20 (and_20_out, not_20_out, B2);
  and and_21 (and_21_out, B2, not_21_out);
  and and_22 (and_22_out, not_22_out, A2);
  and and_23 (and_23_out, A1, not_23_out);
  and and_24 (and_24_out, not_24_out, B1);
  and and_25 (and_25_out, B1, not_25_out);
  and and_26 (and_26_out, not_26_out, A1);
  and and_27 (and_27_out, A0, not_27_out);
  and and_28 (and_28_out, not_28_out, B0);
  and and_29 (and_29_out, B0, not_29_out);
  and and_30 (and_30_out, not_30_out, A0);
  or or_7 (or_7_out, and_14_out, and_12_out);
  or or_8 (or_8_out, and_15_out, and_16_out);
  or or_9 (or_9_out, and_17_out, and_18_out);
  or or_10 (or_10_out, and_19_out, and_20_out);
  or or_11 (or_11_out, and_21_out, and_22_out);
  or or_12 (or_12_out, and_23_out, and_24_out);
  or or_13 (or_13_out, and_25_out, and_26_out);
  or or_14 (or_14_out, and_27_out, and_28_out);
  or or_15 (or_15_out, and_29_out, and_30_out);
  and and_31 (and_31_out, not_31_out, not_32_out, not_33_out, not_34_out);
  and and_32 (and_32_out, or_2_out, or_3_out, or_4_out, or_5_out);
  or or_16 (out_13, undriven_2, or_17_out);
  or or_17 (or_17_out, and_13_out, or_7_out);
  and and_33 (and_33_out, A3, or_8_out);
  and and_34 (and_34_out, B3, or_9_out);
  and and_35 (and_35_out, A2, or_10_out);
  and and_36 (and_36_out, B2, or_11_out);
  and and_37 (and_37_out, A1, or_12_out);
  and and_38 (and_38_out, B1, or_13_out);
  and and_39 (and_39_out, A0, or_14_out);
  and and_40 (and_40_out, B0, or_15_out);
  not not_35 (not_35_out, or_8_out);
  not not_36 (not_36_out, or_8_out);
  not not_37 (not_37_out, or_8_out);
  not not_38 (not_38_out, or_8_out);
  not not_39 (not_39_out, or_8_out);
  not not_40 (not_40_out, or_8_out);
  or or_18 (out_11, and_31_out, and_32_out);
  and and_41 (and_41_out, and_35_out, not_35_out);
  and and_42 (and_42_out, and_36_out, not_36_out);
  and and_43 (and_43_out, and_37_out, not_37_out);
  and and_44 (and_44_out, and_38_out, not_38_out, not_38_out);
  and and_45 (and_45_out, and_39_out, not_39_out);
  and and_46 (and_46_out, and_40_out, not_40_out);
  not not_41 (not_41_out, or_10_out);
  not not_42 (not_42_out, or_10_out);
  not not_43 (not_43_out, or_10_out);
  not not_44 (not_44_out, or_10_out);
  and and_47 (and_47_out, and_43_out, not_41_out);
  and and_48 (and_48_out, and_44_out, not_42_out, not_42_out);
  and and_49 (and_49_out, and_45_out, not_43_out);
  and and_50 (and_50_out, and_46_out, not_44_out);
  not not_45 (not_45_out, or_12_out);
  not not_46 (not_46_out, or_12_out);
  and and_51 (and_51_out, and_49_out, not_45_out);
  and and_52 (and_52_out, and_50_out, not_46_out);
  not not_47 (not_47_out, undriven_5);
  not not_48 (not_48_out, undriven_4);
  or or_19 (or_19_out, and_41_out, or_20_out);
  or or_20 (or_20_out, and_47_out, and_51_out);
  or or_21 (or_21_out, and_48_out, and_52_out);
  and and_53 (and_53_out, undriven_4, not_47_out);
  and and_54 (and_54_out, not_48_out, undriven_5);
  or or_22 (A___B, and_33_out, or_19_out);
  or or_23 (or_23_out, and_42_out, or_21_out);
  or or_24 (or_24_out, and_53_out, and_54_out);
  or or_25 (A___B_2, and_34_out, or_23_out);
  // AND_Gate and_55 has open pins: in0=undriven_3, in4=or_24_out, out=open

  // Notes on the sheet:
  //   A =@! B
endmodule
