// Logisim project D_trigger.circ as structural Verilog: 1 circuit, main circuit main
module main (
  input  DATA,
  input  CLOCK,
  output out_3,
  output out_4
);

  wire and_1_out, and_2_out, and_3_out, and_4_out, not_1_out, not_2_out, not_3_out;

  not not_1 (not_1_out, DATA);
  and and_1 (and_1_out, DATA, CLOCK);
  and and_2 (and_2_out, not_1_out, CLOCK);
  not not_2 (not_2_out, and_1_out);
  not not_3 (not_3_out, and_2_out);
  and and_3 (and_3_out, not_2_out, out_4);
  not not_4 (out_3, and_3_out);
  and and_4 (and_4_out, out_3, not_3_out);
  not not_5 (out_4, and_4_out);
endmodule
