// Logisim project RS_trigger_synch.circ as structural Verilog: 1 circuit, main circuit main
module main (
  input  R,
  input  C,
  input  S,
  output Q,
  output nQ
);

  wire and_1_out, and_2_out, or_1_out, or_2_out;

  and and_1 (and_1_out, R, C);
  and and_2 (and_2_out, C, S);
  or or_1 (or_1_out, and_1_out, nQ);
  or or_2 (or_2_out, Q, and_2_out);
  not not_1 (Q, or_1_out);
  not not_2 (nQ, or_2_out);
endmodule
